// Logisim project sap1p.circ as structural Verilog: 18 circuits, main circuit Clock
module Clock (
  input  SEL,
  input  MAN,
  input  HLT,
  output CLK
);

  wire and_1_out, and_2_out, Clock_out, not_1_out, not_2_out, or_1_out;

  Clock_part Clock (.out(Clock_out));
  not not_1 (not_1_out, HLT);
  not not_2 (not_2_out, SEL);
  and and_1 (and_1_out, SEL, Clock_out);
  and and_2 (and_2_out, MAN, not_2_out);
  or or_1 (or_1_out, and_2_out, and_1_out);
  and and_3 (CLK, or_1_out, not_1_out);
endmodule

module MAIN (
  input  [3:0] ADDR,
  input  [7:0] in_2,
  input  ENABLE,
  input  [7:0] DEBUG
);

  wire alu_1_carry, CLK_clk, P_R_out, ram_1_p_ind, ram_1_r_ind, RSET_out, S_R_out, SET_out, ST_out,
       toggle_1_out, toggle_2_out;
  wire [3:0] addr_reg_1_addr, conrol_1_peek, inst_reg_1_cont_out;
  wire [7:0] alu_1_peek, inst_reg_1_peek, n8bit_reg_1_peek, n8bit_reg_2_peek, output_1_high, output_1_low,
       prog_count_1_peek, ram_1_bus_out, ram_1_peek;
  wire [15:0] conrol_1_contr_out;

  Button S_R (.out(S_R_out));
  Clock CLK (.CLK(CLK_clk), .SEL(toggle_2_out), .MAN(ST_out), .HLT(conrol_1_contr_out[15]));
  TOGGLE toggle_1 (.OUT(toggle_1_out), .BUTTON(P_R_out));
  Button P_R (.out(P_R_out));
  RAM ram_1 (
    .ADDR(addr_reg_1_addr), .P_ADDR(ADDR), .BUS_IN(ram_1_bus_out), .P_IN(in_2), .CLK(CLK_clk),
    .PEEK(ram_1_peek), .BUS_OUT(ram_1_bus_out), .P_R_TOG(toggle_1_out), .P_IND(ram_1_p_ind),
    .R_IND(ram_1_r_ind), .LOAD(conrol_1_contr_out[13]), .SEL(conrol_1_contr_out[12]), .P_SET(SET_out));
  LED led_1 (.in(addr_reg_1_addr[0]));
  LED led_2 (.in(addr_reg_1_addr[2]));
  LED led_3 ();  // open: in
  LED led_4 ();  // open: in
  ADDR_REG addr_reg_1 (.ADDR(addr_reg_1_addr), .CLK(CLK_clk), .BUS_IN(ram_1_bus_out), .LOAD(conrol_1_contr_out[14]));
  INST_REG inst_reg_1 (
    .CLK(CLK_clk), .D(ram_1_bus_out), .BUS_OUT(ram_1_bus_out), .PEEK(inst_reg_1_peek),
    .ENA(conrol_1_contr_out[11]), .LOAD(conrol_1_contr_out[10]), .CONT_OUT(inst_reg_1_cont_out));
  LED led_5 (.in(conrol_1_peek[0]));
  LED led_6 (.in(conrol_1_peek[2]));
  LED led_7 (.in(conrol_1_peek[1]));
  CONROL conrol_1 (
    .CLK(CLK_clk), .INST(inst_reg_1_cont_out), .CONTR_OUT(conrol_1_contr_out), .RSET(RSET_out),
    .PEEK(conrol_1_peek));
  TOGGLE toggle_2 (.OUT(toggle_2_out), .BUTTON(S_R_out));
  LED led_8 (.in(ram_1_p_ind));
  LED led_9 (.in(ram_1_r_ind));
  LED led_10 (.in(inst_reg_1_peek[6]));
  LED led_11 ();  // open: in
  LED led_12 ();  // open: in
  Button ST (.out(ST_out));
  Button SET (.out(SET_out));
  LED led_13 (.in(ram_1_peek[4]));
  LED led_14 (.in(ram_1_peek[6]));
  LED led_15 (.in(ram_1_peek[2]));
  LED led_16 (.in(ram_1_peek[1]));
  LED led_17 (.in(ram_1_peek[5]));
  LED led_18 (.in(ram_1_peek[7]));
  LED led_19 (.in(ram_1_peek[3]));
  LED led_20 (.in(inst_reg_1_peek[2]));
  LED led_21 (.in(inst_reg_1_peek[0]));
  LED led_22 (.in(inst_reg_1_peek[4]));
  LED led_23 ();  // open: in
  LED led_24 ();  // open: in
  Button RSET (.out(RSET_out));
  LED led_25 (.in(CLK_clk));
  ALU alu_1 (
    .A_IN(n8bit_reg_1_peek), .B_IN(n8bit_reg_2_peek), .SUB(conrol_1_contr_out[6]), .BUS_OUT(ram_1_bus_out),
    .EO(conrol_1_contr_out[7]), .PEEK(alu_1_peek), .CARRY(alu_1_carry));
  LED led_26 (.in(ram_1_peek[0]));
  assign ram_1_bus_out = ENABLE ? DEBUG : 8'bz;  // Controlled_Buffer controlled_buffer_1
  LED led_27 (.in(ram_1_bus_out[2]));
  LED led_28 (.in(ram_1_bus_out[4]));
  LED led_29 (.in(ram_1_bus_out[6]));
  LED led_30 (.in(ram_1_bus_out[7]));
  LED led_31 (.in(ram_1_bus_out[3]));
  LED led_32 (.in(ram_1_bus_out[5]));
  // Probe on prog_count_1_peek
  PROG_COUNT prog_count_1 (
    .LOAD_JMP(conrol_1_contr_out[1]), .B_IN(ram_1_bus_out), .INC(conrol_1_contr_out[3]), .CLK(CLK_clk),
    .RSET(RSET_out), .ENA(conrol_1_contr_out[2]), .PEEK(prog_count_1_peek), .B_OUT(ram_1_bus_out),
    .J_C(conrol_1_contr_out[0]), .CARRY(alu_1_carry));
  LED led_33 (.in(n8bit_reg_1_peek[2]));
  LED led_34 (.in(n8bit_reg_1_peek[6]));
  LED led_35 (.in(n8bit_reg_1_peek[4]));
  LED led_36 (.in(n8bit_reg_1_peek[7]));
  LED led_37 (.in(n8bit_reg_1_peek[3]));
  LED led_38 (.in(n8bit_reg_1_peek[1]));
  LED led_39 (.in(n8bit_reg_1_peek[5]));
  _8BIT_REG u_8bit_reg_1 (
    .CLK(CLK_clk), .ENA(conrol_1_contr_out[8]), .LOAD(conrol_1_contr_out[9]), .IN(ram_1_bus_out),
    .PEEK(n8bit_reg_1_peek), .OUT(ram_1_bus_out), .RSET(RSET_out));
  LED led_40 (.in(alu_1_peek[2]));
  LED led_41 (.in(alu_1_peek[4]));
  LED led_42 (.in(alu_1_peek[6]));
  LED led_43 (.in(alu_1_peek[3]));
  LED led_44 (.in(alu_1_peek[5]));
  LED led_45 (.in(alu_1_peek[7]));
  LED led_46 (.in(alu_1_peek[1]));
  LED led_47 (.in(n8bit_reg_2_peek[4]));
  LED led_48 (.in(n8bit_reg_2_peek[2]));
  LED led_49 (.in(n8bit_reg_2_peek[6]));
  LED led_50 (.in(n8bit_reg_2_peek[1]));
  LED led_51 (.in(n8bit_reg_2_peek[7]));
  LED led_52 (.in(n8bit_reg_2_peek[5]));
  LED led_53 (.in(n8bit_reg_2_peek[3]));
  _8BIT_REG u_8bit_reg_2 (
    .CLK(CLK_clk), .ENA(1'b0), .LOAD(conrol_1_contr_out[5]), .IN(ram_1_bus_out), .PEEK(n8bit_reg_2_peek),
    .OUT(ram_1_bus_out), .RSET(RSET_out));
  OUTPUT output_1 (
    .CLK(CLK_clk), .BUS(ram_1_bus_out), .LOAD(conrol_1_contr_out[4]), .LOW(output_1_low),
    .HIGH(output_1_high), .in_3(RSET_out));
  LED led_54 (.in(ram_1_bus_out[0]));
  LED led_55 (.in(ram_1_bus_out[1]));
  LED led_56 (.in(prog_count_1_peek[2]));
  LED led_57 (.in(prog_count_1_peek[0]));
  LED led_58 (.in(prog_count_1_peek[3]));
  LED led_59 (.in(prog_count_1_peek[1]));
  LED led_60 (.in(n8bit_reg_1_peek[0]));
  LED led_61 (.in(alu_1_peek[0]));
  LED led_62 (.in(n8bit_reg_2_peek[0]));
  _7_Segment_Display u_7_segment_display_1 (
    .g(output_1_low[7]), .f(output_1_low[6]), .a(output_1_low[5]), .b(output_1_low[4]), .e(output_1_low[0]),
    .d(output_1_low[1]), .c(output_1_low[2]), .dp(output_1_low[3]));
  LED led_63 (.in(conrol_1_contr_out[2]));
  LED led_64 (.in(conrol_1_contr_out[4]));
  LED led_65 (.in(conrol_1_contr_out[6]));
  LED led_66 (.in(conrol_1_contr_out[0]));
  LED led_67 (.in(conrol_1_contr_out[3]));
  LED led_68 (.in(conrol_1_contr_out[1]));
  LED led_69 (.in(conrol_1_contr_out[5]));
  LED led_70 (.in(conrol_1_contr_out[7]));
  LED led_71 (.in(conrol_1_contr_out[10]));
  LED led_72 (.in(conrol_1_contr_out[12]));
  LED led_73 (.in(conrol_1_contr_out[8]));
  LED led_74 (.in(conrol_1_contr_out[14]));
  LED led_75 (.in(conrol_1_contr_out[11]));
  LED led_76 (.in(conrol_1_contr_out[9]));
  LED led_77 (.in(conrol_1_contr_out[15]));
  LED led_78 (.in(conrol_1_contr_out[13]));
  _7_Segment_Display u_7_segment_display_2 (
    .g(output_1_high[7]), .f(output_1_high[6]), .a(output_1_high[5]), .b(output_1_high[4]),
    .e(output_1_high[0]), .d(output_1_high[1]), .c(output_1_high[2]), .dp(output_1_high[3]));

  // Notes on the sheet:
  //   STEP/RUN TOGGLE
  //   SAP-1 Plus 8-Bit Computer
  //   PROGRAM INTERFACE
  //   PROG
  //   RUN
  //   BUS
  //   CLOCK
  //   REGISTER A
  //   REGISTER B
endmodule

module d_latch (
  input  CLK,
  input  LOAD,
  input  D,
  output Q
);

  wire and_1_out, and_2_out, and_3_out, and_4_out, nor_2_out, not_1_out, not_2_out, or_1_out;

  not not_1 (not_1_out, LOAD);
  and and_1 (and_1_out, Q, not_1_out);
  and and_2 (and_2_out, LOAD, D);
  not not_2 (not_2_out, or_1_out);
  or or_1 (or_1_out, and_1_out, and_2_out);
  and and_3 (and_3_out, not_2_out, CLK);
  and and_4 (and_4_out, CLK, or_1_out);
  nor nor_1 (Q, and_3_out, nor_2_out);
  nor nor_2 (nor_2_out, Q, and_4_out);

  // Notes on the sheet:
  //   LOAD LOGIC
  //   D FLIP-FLOP
endmodule

module PC (
);

  wire undriven;
  wire [3:0] controlled_buffer_1_out, counter_1_q;

  assign controlled_buffer_1_out = undriven ? counter_1_q : 4'bz;  // Controlled_Buffer controlled_buffer_1
  Counter #(.width(4), .max('hf)) counter_1 (.Q(counter_1_q));  // open: load, D, count, carry, clk, clr
endmodule

module _1BIT (
  input  ENA,
  input  CLK,
  input  LOAD,
  input  IN,
  output OUT,
  output PEEK
);

  wire and_1_out, and_2_out, and_3_out, and_4_out, and_5_out, nor_2_out, not_1_out, not_2_out, not_3_out,
       or_1_out;

  not not_1 (not_1_out, ENA);
  and and_1 (and_1_out, not_1_out, LOAD);
  not not_2 (not_2_out, and_1_out);
  and and_2 (and_2_out, PEEK, not_2_out);
  and and_3 (and_3_out, and_1_out, IN);
  or or_1 (or_1_out, and_2_out, and_3_out);
  not not_3 (not_3_out, or_1_out);
  and and_4 (and_4_out, not_3_out, CLK);
  and and_5 (and_5_out, CLK, or_1_out);
  nor nor_1 (PEEK, and_4_out, nor_2_out);
  nor nor_2 (nor_2_out, PEEK, and_5_out);
  assign OUT = ENA ? PEEK : 1'bz;  // Controlled_Buffer controlled_buffer_1

  // Notes on the sheet:
  //   LOAD LOGIC
  //   D FLIP-FLOP
endmodule

module _8BIT_REG (
  input  ENA,
  input  [7:0] IN,
  input  LOAD,
  input  CLK,
  input  RSET,
  output [7:0] OUT,
  output [7:0] PEEK
);

  wire undriven_2, undriven_3, undriven_4;
  wire [7:0] n1bit_8_out, n1bit_8_peek, undriven;

  _1BIT u_1bit_1 (
    .CLK(undriven_4), .LOAD(undriven_2), .IN(undriven[7]), .OUT(n1bit_8_out[7]), .PEEK(n1bit_8_peek[7]),
    .ENA(undriven_3));
  _1BIT u_1bit_2 (
    .CLK(undriven_4), .LOAD(undriven_2), .IN(undriven[6]), .OUT(n1bit_8_out[6]), .PEEK(n1bit_8_peek[6]),
    .ENA(undriven_3));
  _1BIT u_1bit_3 (
    .CLK(undriven_4), .LOAD(undriven_2), .IN(undriven[5]), .OUT(n1bit_8_out[5]), .PEEK(n1bit_8_peek[5]),
    .ENA(undriven_3));
  _1BIT u_1bit_4 (
    .CLK(undriven_4), .LOAD(undriven_2), .IN(undriven[4]), .OUT(n1bit_8_out[4]), .PEEK(n1bit_8_peek[4]),
    .ENA(undriven_3));
  _1BIT u_1bit_5 (
    .CLK(undriven_4), .LOAD(undriven_2), .IN(undriven[3]), .OUT(n1bit_8_out[3]), .PEEK(n1bit_8_peek[3]),
    .ENA(undriven_3));
  _1BIT u_1bit_6 (
    .CLK(undriven_4), .LOAD(undriven_2), .IN(undriven[2]), .OUT(n1bit_8_out[2]), .PEEK(n1bit_8_peek[2]),
    .ENA(undriven_3));
  _1BIT u_1bit_7 (
    .CLK(undriven_4), .LOAD(undriven_2), .IN(undriven[1]), .OUT(n1bit_8_out[1]), .PEEK(n1bit_8_peek[1]),
    .ENA(undriven_3));
  _1BIT u_1bit_8 (
    .CLK(undriven_4), .LOAD(undriven_2), .IN(undriven[0]), .OUT(n1bit_8_out[0]), .PEEK(n1bit_8_peek[0]),
    .ENA(undriven_3));
  Register register_1 (.D(IN), .en(LOAD), .Q(PEEK), .clk(CLK), .clr(RSET));
  assign OUT = ENA ? PEEK : 8'bz;  // Controlled_Buffer controlled_buffer_1

  // Notes on the sheet:
  //   LOAD
  //   CLK
  //   ENA
  //   IN
  //   NOTE - oscilation problem w/ my 1bit registers (?)
  //   OUT
  //   PEEK
endmodule

module INST_REG (
  input  CLK,
  input  ENA,
  input  [7:0] D,
  input  LOAD,
  output [7:0] PEEK,
  output [7:0] BUS_OUT,
  output [3:0] CONT_OUT
);

  assign BUS_OUT = ENA ? {4'b0000, PEEK[3:0]} : 8'bz;  // Controlled_Buffer controlled_buffer_1
  _8BIT_REG u_8bit_reg_1 (.CLK(CLK), .ENA(ENA), .LOAD(LOAD), .IN(D), .PEEK({CONT_OUT, PEEK[3:0]}));  // open: OUT, RSET

  assign PEEK[7:4] = CONT_OUT;
endmodule

module _1B_AD (
  input  A_IN,
  input  B_IN,
  input  CARRRY_IN,
  output OUT,
  output CARRY_OUT
);

  wire and_1_out, and_2_out, xor_1_out;

  xor xor_1 (xor_1_out, A_IN, B_IN);
  xor xor_2 (OUT, xor_1_out, CARRRY_IN);
  and and_1 (and_1_out, xor_1_out, CARRRY_IN);
  or or_1 (CARRY_OUT, and_1_out, and_2_out);
  and and_2 (and_2_out, A_IN, B_IN);
endmodule

module ALU (
  input  [7:0] A_IN,
  input  [7:0] B_IN,
  input  EO,
  input  SUB,
  output [7:0] PEEK,
  output [7:0] BUS_OUT,
  output CARRY
);

  wire n4b_ad_1_carry_out;
  wire [7:0] n8b_inv_1_out;

  _8B_INV u_8b_inv_1 (.IN(B_IN), .INV(SUB), .OUT(n8b_inv_1_out));
  _4B_AD u_4b_ad_1 (
    .CARRY_IN(SUB), .A(A_IN[3:0]), .B(n8b_inv_1_out[3:0]), .OUT(PEEK[3:0]), .CARRY_OUT(n4b_ad_1_carry_out));
  _4B_AD u_4b_ad_2 (
    .CARRY_IN(n4b_ad_1_carry_out), .A(A_IN[7:4]), .B(n8b_inv_1_out[7:4]), .OUT(PEEK[7:4]), .CARRY_OUT(CARRY));
  assign BUS_OUT = EO ? PEEK : 8'bz;  // Controlled_Buffer controlled_buffer_1
endmodule

module _8B_INV (
  input  [7:0] IN,
  input  INV,
  output [7:0] OUT
);

  xor xor_1 (OUT[0], IN[0], INV);
  xor xor_2 (OUT[1], IN[1], INV);
  xor xor_3 (OUT[2], IN[2], INV);
  xor xor_4 (OUT[3], IN[3], INV);
  xor xor_5 (OUT[4], IN[4], INV);
  xor xor_6 (OUT[5], IN[5], INV);
  xor xor_7 (OUT[6], IN[6], INV);
  xor xor_8 (OUT[7], IN[7], INV);
endmodule

module RAM (
  input  P_R_TOG,
  input  [3:0] ADDR,
  input  [3:0] P_ADDR,
  input  [7:0] BUS_IN,
  input  [7:0] P_IN,
  input  SEL,
  input  CLK,
  input  P_SET,
  input  LOAD,
  output P_IND,
  output R_IND,
  output [7:0] PEEK,
  output [7:0] BUS_OUT
);

  wire and_1_out, clock_1_out, not_2_out, or_1_out, or_2_out;
  wire [3:0] multiplexer_1_out;
  wire [7:0] multiplexer_2_out;

  Clock_part clock_1 (.out(clock_1_out));
  not not_1 (R_IND, P_R_TOG);
  Multiplexer #(.width(4)) multiplexer_1 (
    .in0(ADDR), .in1(P_ADDR), .out(multiplexer_1_out), .sel(P_R_TOG));  // open: en
  Multiplexer #(.width(8)) multiplexer_2 (
    .in0(BUS_IN), .in1(P_IN), .out(multiplexer_2_out), .sel(P_R_TOG));  // open: en
  assign PEEK = or_2_out ? multiplexer_2_out : 8'bz;  // Controlled_Buffer controlled_buffer_1
  and and_1 (and_1_out, clock_1_out, P_SET);
  or or_1 (or_1_out, CLK, and_1_out);
  or or_2 (or_2_out, P_SET, LOAD);
  not not_2 (not_2_out, or_2_out);
  RAM_part #(.addrWidth(4), .dataWidth(4)) ram_1 (
    .addr(multiplexer_1_out), .data(PEEK[3:0]), .clk(or_1_out), .ld(not_2_out));  // open: sel, clr
  RAM_part #(.addrWidth(4), .dataWidth(4)) ram_2 (
    .addr(multiplexer_1_out), .data(PEEK[7:4]), .clk(or_1_out), .ld(not_2_out));  // open: sel, clr
  // Probe on PEEK[7:4]
  assign BUS_OUT = SEL ? PEEK : 8'bz;  // Controlled_Buffer controlled_buffer_2

  assign P_IND = P_R_TOG;
endmodule

module TOGGLE (
  input  BUTTON,
  output OUT
);

  J_K_Flip_Flop j_k_ff_1 (.J(BUTTON), .clk(BUTTON), .K(BUTTON), .Q(OUT));  // open: Qn, preset, en, reset
endmodule

module PROG_COUNT (
  input  J_C,
  input  CARRY,
  input  LOAD_JMP,
  input  [7:0] B_IN,
  input  INC,
  input  CLK,
  input  RSET,
  input  ENA,
  output [7:0] PEEK,
  output [7:0] B_OUT
);

  wire and_1_out, or_1_out;

  and and_1 (and_1_out, J_C, CARRY);
  or or_1 (or_1_out, and_1_out, LOAD_JMP);
  Counter #(.width(4), .max('hf)) counter_1 (
    .load(or_1_out), .D(B_IN[3:0]), .count(INC), .Q(PEEK[3:0]), .clk(CLK), .clr(RSET));  // open: carry
  assign B_OUT = ENA ? {4'b0000, PEEK[3:0]} : 8'bz;  // Controlled_Buffer controlled_buffer_1

  assign PEEK[7:4] = 4'b0000;
endmodule

module scratch (
  input  in_1,
  input  in_2,
  input  RSET
);

  wire [3:0] counter_1_q;
  wire [7:0] rom_1_data, undriven;

  Counter #(.width(4), .max('hf)) counter_1 (
    .count(in_1), .Q(counter_1_q), .clk(in_2), .clr(RSET));  // open: load, D, carry
  _7_Segment_Display #(.active("false")) u_7_segment_display_1 (
    .g(undriven[7]), .f(undriven[6]), .a(undriven[5]), .b(undriven[4]), .e(undriven[0]), .d(undriven[1]),
    .c(undriven[2]), .dp(undriven[3]));
  ROM rom_1 (.addr({4'b0000, counter_1_q}), .data(rom_1_data));  // open: sel
  _7_Segment_Display u_7_segment_display_2 (
    .g(rom_1_data[7]), .f(rom_1_data[6]), .a(rom_1_data[5]), .b(rom_1_data[4]), .e(rom_1_data[0]),
    .d(rom_1_data[1]), .c(rom_1_data[2]), .dp(rom_1_data[3]));

  // Notes on the sheet:
  //   contents of rom_1 (hex, n*v repeats v):
  //   77 14 b3 b6 d4 e6 e7 34 f7 f4 f5 c7 63 97 e3 e1
endmodule

module _4B_AD (
  input  CARRY_IN,
  input  [3:0] A,
  input  [3:0] B,
  output [3:0] OUT,
  output CARRY_OUT
);

  wire n1b_ad_1_carry_out, n1b_ad_2_carry_out, n1b_ad_3_carry_out;

  _1B_AD u_1b_ad_1 (.A_IN(A[0]), .B_IN(B[0]), .CARRRY_IN(CARRY_IN), .OUT(OUT[0]), .CARRY_OUT(n1b_ad_1_carry_out));
  _1B_AD u_1b_ad_2 (
    .A_IN(A[1]), .B_IN(B[1]), .CARRRY_IN(n1b_ad_1_carry_out), .OUT(OUT[1]), .CARRY_OUT(n1b_ad_2_carry_out));
  _1B_AD u_1b_ad_3 (
    .A_IN(A[2]), .B_IN(B[2]), .CARRRY_IN(n1b_ad_2_carry_out), .OUT(OUT[2]), .CARRY_OUT(n1b_ad_3_carry_out));
  _1B_AD u_1b_ad_4 (.A_IN(A[3]), .B_IN(B[3]), .CARRRY_IN(n1b_ad_3_carry_out), .OUT(OUT[3]), .CARRY_OUT(CARRY_OUT));
endmodule

module CONROL (
  input  CLK,
  input  RSET,
  input  [3:0] INST,
  output [3:0] PEEK,
  output [15:0] CONTR_OUT
);

  wire comparator_1_eq, not_1_out, or_1_out;

  not not_1 (not_1_out, CLK);
  Comparator #(.width(4)) comparator_1 (.a(PEEK), .b(4'b0101), .eq(comparator_1_eq));  // open: gt, lt
  Counter #(.width(4), .max('hf)) counter_1 (.Q(PEEK), .clk(not_1_out), .clr(or_1_out));  // open: load, D, count, carry
  or or_1 (or_1_out, comparator_1_eq, RSET);
  // Probe on {INST, PEEK}
  ROM #(.dataWidth(16)) rom_1 (.addr({INST, PEEK}), .data(CONTR_OUT));  // open: sel

  // Notes on the sheet:
  //   NOTE - invert clock sigmal to change between ticks
  //   contents of rom_1 (hex, n*v repeats v):
  //   4004 1408 14*0 4004 1408 4800 1200 12*0 4004 1408 4800 1020 280 11*0 4004 1408 4800 1020 2c0 11*0
  //   4004 1408 4800 2100 12*0 4004 1408 14*0 4004 1408 802 13*0 4004 1408 a00 13*0 4004 1408 801 13*0
  //   4004 1408 14*0 4004 1408 14*0 4004 1408 14*0 4004 1408 14*0 4004 1408 14*0 4004 1408 110 13*0 4004
  //   1408 8000
endmodule

module OUTPUT (
  input  CLK,
  input  [7:0] BUS,
  input  in_3,
  input  LOAD,
  output [7:0] LOW,
  output [7:0] HIGH
);

  wire [7:0] n8bit_reg_1_peek;

  _8BIT_REG u_8bit_reg_1 (.CLK(CLK), .LOAD(LOAD), .IN(BUS), .PEEK(n8bit_reg_1_peek), .RSET(in_3));  // open: ENA, OUT
  ROM rom_1 (.addr({4'b0000, n8bit_reg_1_peek[7:4]}), .data(LOW));  // open: sel
  ROM rom_2 (.addr({4'b0000, n8bit_reg_1_peek[3:0]}), .data(HIGH));  // open: sel

  // Notes on the sheet:
  //   contents of rom_1 (hex, n*v repeats v):
  //   77 14 b3 b6 d4 e6 e7 34 f7 f4 f5 c7 63 97 e3 e1
  //   contents of rom_2 (hex, n*v repeats v):
  //   77 14 b3 b6 d4 e6 e7 34 f7 f4 f5 c7 63 97 e3 e1
endmodule

module ADDR_REG (
  input  CLK,
  input  [7:0] BUS_IN,
  input  LOAD,
  output [3:0] ADDR
);

  wire [3:0] n8bit_reg_1_out, n8bit_reg_1_out_2, n8bit_reg_1_peek;

  _8BIT_REG u_8bit_reg_1 (
    .CLK(CLK), .ENA(1'b0), .LOAD(LOAD), .IN(BUS_IN), .PEEK({n8bit_reg_1_peek, ADDR}),
    .OUT({n8bit_reg_1_out_2, n8bit_reg_1_out}));  // open: RSET
endmodule
